# Fritzing sketch muse (saved by Fritzing 0.9.3b)
breadboards: 1

parts:
  Part5 = RedBear-Duo
  S1 = Pushbutton [package="[THT]"]
  S2 = Pushbutton [package="[THT]"]
  S3 = Pushbutton [package="[THT]"]
  S4 = Pushbutton [package="[THT]"]
  R1 = Rotary Potentiometer (Small) [maximum_resistance=100kΩ package=THT]
  R2 = Rotary Potentiometer (Small) [maximum_resistance=100kΩ package=THT]
  R3 = Rotary Potentiometer (Small) [maximum_resistance=100kΩ package=THT]
  R4 = Rotary Potentiometer (Small) [maximum_resistance=100kΩ package=THT]
  U2 = SLIDER [package=slider]

nets:
  N1: Part5.A0, R4.wiper
  N2: Part5.A1, R3.wiper
  N3: Part5.A2, R2.wiper
  N4: Part5.A3, R1.wiper
  N5: Part5.A4, U2.S
  N6: Part5.GND, S1.Pin_1, S1.Pin_2, S2.Pin_1, S2.Pin_2, S3.Pin_1, S3.Pin_2, S4.Pin_1, S4.Pin_2, R1.leg1, R2.leg1, R3.leg1, R4.leg1, U2.E
  N7: Part5.D0, S4.Pin_3, S4.Pin_4
  N8: Part5.D1, S3.Pin_3, S3.Pin_4
  N9: Part5.D2, S2.Pin_3, S2.Pin_4
  N10: Part5.D3, S1.Pin_3, S1.Pin_4
  N11: Part5.3V3, R1.leg2, R2.leg2, R3.leg2, R4.leg2, U2.A

custom parts:
  RedBear-Duo: Duo is a thumb-size development board made to simplify the building process of Internet of Things (IoT). This part is a modification of the Particle Photon part by Brett Walach,Fabian Althaus
